// Logisim project Data Path.circ as structural Verilog: 5 circuits, main circuit main
module main (
  input  Reset,
  output [9:0] Result_Checker,
  output out_3,
  output [1:0] out_4
);

  wire alu_10_bit_1_zero, and_1_out, Clock_out, controller_1_alu_src, controller_1_bi_cin,
       controller_1_brunch, controller_1_jump, controller_1_mem_r, controller_1_mem_to_reg,
       controller_1_mem_w, controller_1_reg_dst, controller_1_reg_w, not_1_out, or_1_out;
  wire [1:0] multiplexer_1_out;
  wire [9:0] adder_1_out, adder_2_out, bit_extender_1_out, bit_extender_2_out, multiplexer_2_out,
       multiplexer_3_out, multiplexer_4_out, multiplexer_5_out, PC_q, ram_1_data, register_file_1_out_7,
       register_file_1_out_8, rom_1_data, shifter_1_out, shifter_2_out;

  Clock #(.lowDuration(4)) Clock (.out(Clock_out));
  Register #(.width(10)) PC (.D(multiplexer_5_out), .Q(PC_q), .clk(Clock_out), .clr(Reset));  // open: en
  Adder #(.width(10)) adder_1 (.a(10'h2), .b(PC_q), .out(adder_1_out));  // open: cin, cout
  not not_1 (not_1_out, Clock_out);
  ROM #(.addrWidth(10), .dataWidth(10)) rom_1 (.addr(PC_q), .data(rom_1_data));  // open: sel
  assign bit_extender_1_out = {{7{1'b0}}, rom_1_data[2:0]};  // Bit_Extender bit_extender_1
  Controller controller_1 (
    .Op3(rom_1_data[9]), .Op2(rom_1_data[8]), .Op1(rom_1_data[7]), .Reg_dst(controller_1_reg_dst),
    .Reg_W(controller_1_reg_w), .ALU_Src(controller_1_alu_src), .ALU_Op2(out_4[1]), .ALU_Op1(out_4[0]),
    .Mem_R(controller_1_mem_r), .Mem_W(controller_1_mem_w), .Mem_to_Reg(controller_1_mem_to_reg),
    .Bi_Cin(controller_1_bi_cin), .Brunch(controller_1_brunch), .Jump(controller_1_jump));
  assign bit_extender_2_out = {{3{1'b0}}, rom_1_data[6:0]};  // Bit_Extender bit_extender_2
  Multiplexer #(.width(2), .enable("false")) multiplexer_1 (
    .in0(rom_1_data[2:1]), .in1(rom_1_data[4:3]), .out(multiplexer_1_out), .sel(controller_1_reg_dst));
  Shifter #(.width(10)) shifter_1 (.in(bit_extender_2_out), .\dist (4'b0001), .out(shifter_1_out));
  Register_File register_file_1 (
    .Write_Data(multiplexer_3_out), .out_7(register_file_1_out_7), .out_8(register_file_1_out_8),
    .RD(multiplexer_1_out), .RS(rom_1_data[6:5]), .RT(rom_1_data[4:3]), .in_6(controller_1_reg_w),
    .clock(not_1_out));
  Multiplexer #(.width(10), .enable("false")) multiplexer_2 (
    .in0(register_file_1_out_8), .in1(bit_extender_1_out), .out(multiplexer_2_out), .sel(controller_1_alu_src));
  Shifter #(.width(10)) shifter_2 (.in(bit_extender_1_out), .\dist (4'b0001), .out(shifter_2_out));
  Adder #(.width(10)) adder_2 (.a(adder_1_out), .b(shifter_2_out), .out(adder_2_out));  // open: cin, cout
  ALU_10_Bit alu_10_bit_1 (
    .A(register_file_1_out_7), .Cout(out_3), .Zero(alu_10_bit_1_zero), .B(multiplexer_2_out), .OP(out_4),
    .out_5(Result_Checker), .Bi(controller_1_bi_cin));
  Multiplexer #(.width(10), .enable("false")) multiplexer_3 (
    .in0(Result_Checker), .in1(ram_1_data), .out(multiplexer_3_out), .sel(controller_1_mem_to_reg));
  Multiplexer #(.width(10), .enable("false")) multiplexer_4 (
    .in0(adder_1_out), .in1(adder_2_out), .out(multiplexer_4_out), .sel(and_1_out));
  and and_1 (and_1_out, alu_10_bit_1_zero, controller_1_brunch);
  or or_1 (or_1_out, controller_1_mem_w, controller_1_mem_r);
  Multiplexer #(.width(10), .enable("false")) multiplexer_5 (
    .in0(multiplexer_4_out), .in1(shifter_1_out), .out(multiplexer_5_out), .sel(controller_1_jump));
  RAM #(.addrWidth(10), .dataWidth(10), .bus("separate")) ram_1 (
    .addr(Result_Checker), .din(register_file_1_out_8), .data(ram_1_data), .str(controller_1_mem_w),
    .sel(or_1_out), .clk(not_1_out), .ld(controller_1_mem_r));  // open: clr

  // Notes on the sheet:
  //   Instruction Memory
  //   contents of rom_1 (hex, n*v repeats v):
  //   182 0 1aa 0 8 0 2e0 0 268
  //   Memory
endmodule

module Register_File (
  input  [9:0] Write_Data,
  input  [1:0] RS,
  input  [1:0] RD,
  input  [1:0] RT,
  input  clock,
  input  in_6,
  output [9:0] out_7,
  output [9:0] out_8
);

  wire and_1_out, decoder_1_out0, decoder_1_out1, decoder_1_out2;
  wire [9:0] t0_q, t1_q, t2_q;

  Decoder #(.select(2), .enable("false")) decoder_1 (
    .out0(decoder_1_out0), .out1(decoder_1_out1), .out2(decoder_1_out2), .sel(RD));  // open: out3
  and and_1 (and_1_out, clock, in_6);
  Register #(.width(10)) t0 (.D(Write_Data), .en(decoder_1_out0), .Q(t0_q), .clk(and_1_out));  // open: clr
  Register #(.width(10)) t1 (.D(Write_Data), .en(decoder_1_out1), .Q(t1_q), .clk(and_1_out));  // open: clr
  Register #(.width(10)) t2 (.D(Write_Data), .en(decoder_1_out2), .Q(t2_q), .clk(and_1_out));  // open: clr
  Multiplexer #(.select(2), .width(10), .enable("false")) multiplexer_1 (
    .in0(t0_q), .in1(t1_q), .in2(t2_q), .in3({10{1'b0}}), .out(out_7), .sel(RS));
  Multiplexer #(.select(2), .width(10), .enable("false")) multiplexer_2 (
    .in0(t0_q), .in1(t1_q), .in2(t2_q), .in3({10{1'b0}}), .out(out_8), .sel(RT));
endmodule

module ALU_1_bit (
  input  Cin,
  input  A0,
  input  B0,
  input  Bi,
  input  [1:0] in_5,
  output result,
  output carry
);

  wire adder_1_out, and_1_out, multiplexer_1_out, not_1_out, or_1_out;

  Multiplexer #(.enable("false")) multiplexer_1 (.in0(B0), .in1(not_1_out), .out(multiplexer_1_out), .sel(Bi));
  not not_1 (not_1_out, B0);
  and and_1 (and_1_out, A0, B0);
  or or_1 (or_1_out, A0, B0);
  Adder #(.width(1)) adder_1 (.a(A0), .b(multiplexer_1_out), .out(adder_1_out), .cin(Cin), .cout(carry));
  Multiplexer #(.select(2), .enable("false")) multiplexer_2 (
    .in0(and_1_out), .in1(or_1_out), .in2(adder_1_out), .out(result), .sel(in_5));  // open: in3
endmodule

module ALU_10_Bit (
  input  Bi,
  input  [1:0] OP,
  input  [9:0] A,
  input  [9:0] B,
  output [9:0] out_5,
  output Cout,
  output Zero
);

  wire alu_1_bit_1_carry, alu_1_bit_2_carry, alu_1_bit_3_carry, alu_1_bit_4_carry, alu_1_bit_5_carry,
       alu_1_bit_6_carry, alu_1_bit_7_carry, alu_1_bit_8_carry, alu_1_bit_9_carry;

  ALU_1_bit alu_1_bit_1 (
    .A0(A[0]), .B0(B[0]), .result(out_5[0]), .carry(alu_1_bit_1_carry), .Cin(Bi), .Bi(Bi), .in_5(OP));
  ALU_1_bit alu_1_bit_2 (
    .A0(A[1]), .B0(B[1]), .result(out_5[1]), .carry(alu_1_bit_2_carry), .Cin(alu_1_bit_1_carry), .Bi(Bi),
    .in_5(OP));
  ALU_1_bit alu_1_bit_3 (
    .A0(A[2]), .B0(B[2]), .result(out_5[2]), .carry(alu_1_bit_3_carry), .Cin(alu_1_bit_2_carry), .Bi(Bi),
    .in_5(OP));
  ALU_1_bit alu_1_bit_4 (
    .A0(A[3]), .B0(B[3]), .result(out_5[3]), .carry(alu_1_bit_4_carry), .Cin(alu_1_bit_3_carry), .Bi(Bi),
    .in_5(OP));
  ALU_1_bit alu_1_bit_5 (
    .A0(A[4]), .B0(B[4]), .result(out_5[4]), .carry(alu_1_bit_5_carry), .Cin(alu_1_bit_4_carry), .Bi(Bi),
    .in_5(OP));
  ALU_1_bit alu_1_bit_6 (
    .A0(A[5]), .B0(B[5]), .result(out_5[6]), .carry(alu_1_bit_6_carry), .Cin(alu_1_bit_5_carry), .Bi(Bi),
    .in_5(OP));
  ALU_1_bit alu_1_bit_7 (
    .A0(A[6]), .B0(B[6]), .result(out_5[6]), .carry(alu_1_bit_7_carry), .Cin(alu_1_bit_6_carry), .Bi(Bi),
    .in_5(OP));
  ALU_1_bit alu_1_bit_8 (
    .A0(A[7]), .B0(B[7]), .result(out_5[7]), .carry(alu_1_bit_8_carry), .Cin(alu_1_bit_7_carry), .Bi(Bi),
    .in_5(OP));
  ALU_1_bit alu_1_bit_9 (
    .A0(A[8]), .B0(B[8]), .result(out_5[8]), .carry(alu_1_bit_9_carry), .Cin(alu_1_bit_8_carry), .Bi(Bi),
    .in_5(OP));
  ALU_1_bit alu_1_bit_10 (
    .A0(A[9]), .B0(B[9]), .result(out_5[9]), .carry(Cout), .Cin(alu_1_bit_9_carry), .Bi(Bi), .in_5(OP));
  nor nor_1 (Zero, out_5[0], out_5[1], out_5[2], out_5[3], out_5[4], out_5[6], out_5[6], out_5[7], out_5[8], out_5[9]);

  assign out_5[5] = out_5[6];

  // Notes on the sheet:
  //   cin
endmodule

module Controller (
  input  Op3,
  input  Op2,
  input  Op1,
  output Reg_dst,
  output Reg_W,
  output ALU_Src,
  output ALU_Op2,
  output ALU_Op1,
  output Mem_R,
  output Mem_W,
  output Mem_to_Reg,
  output Bi_Cin,
  output Brunch,
  output Jump
);

  wire and_2_out, and_3_out, and_4_out, and_5_out, and_6_out, and_7_out, and_8_out, and_9_out, and_10_out,
       not_1_out, not_2_out, not_3_out, not_4_out, not_5_out, not_6_out, not_7_out, not_8_out, not_9_out,
       not_10_out, not_11_out, not_12_out, not_13_out, not_14_out, not_15_out, not_16_out, not_17_out,
       not_18_out, not_19_out, not_20_out, not_21_out, not_22_out;

  not not_1 (not_1_out, Op3);
  not not_2 (not_2_out, Op2);
  not not_3 (not_3_out, Op1);
  not not_4 (not_4_out, Op2);
  not not_5 (not_5_out, Op1);
  not not_6 (not_6_out, Op3);
  not not_7 (not_7_out, Op2);
  not not_8 (not_8_out, Op2);
  not not_9 (not_9_out, Op1);
  not not_10 (not_10_out, Op3);
  not not_11 (not_11_out, Op2);
  not not_12 (not_12_out, Op1);
  not not_13 (not_13_out, Op3);
  not not_14 (not_14_out, Op1);
  not not_15 (not_15_out, Op2);
  not not_16 (not_16_out, Op1);
  not not_17 (not_17_out, Op2);
  not not_18 (not_18_out, Op2);
  not not_19 (not_19_out, Op1);
  not not_20 (not_20_out, Op1);
  not not_21 (not_21_out, Op1);
  and and_1 (Jump, Op3, Op2, Op1);
  and and_2 (and_2_out, not_1_out, Op2, Op1);
  and and_3 (and_3_out, Op3, not_2_out, not_3_out);
  not not_22 (not_22_out, Op3);
  and and_4 (and_4_out, not_4_out, not_5_out);
  and and_5 (and_5_out, not_6_out, Op2, Op1);
  and and_6 (and_6_out, Op3, not_7_out);
  and and_7 (and_7_out, not_8_out, not_9_out);
  and and_8 (and_8_out, not_10_out, Op2, Op1);
  and and_9 (and_9_out, Op3, not_11_out);
  and and_10 (and_10_out, Op3, not_12_out);
  and and_11 (ALU_Op1, not_13_out, Op2, not_14_out);
  and and_12 (Mem_R, Op3, not_15_out, not_16_out);
  and and_13 (Mem_W, Op3, not_17_out, Op1);
  and and_14 (Mem_to_Reg, Op3, not_18_out, not_19_out);
  and and_15 (Bi_Cin, Op3, Op2, not_20_out);
  and and_16 (Brunch, Op3, Op2, not_21_out);
  or or_1 (Reg_dst, and_2_out, and_3_out);
  or or_2 (Reg_W, not_22_out, and_4_out);
  or or_3 (ALU_Src, and_5_out, and_6_out);
  or or_4 (ALU_Op2, and_7_out, and_8_out, and_9_out, and_10_out);
endmodule
